// Logisim project TP3-3.circ as structural Verilog: 1 circuit, main circuit main
module main (
  input  in_1,
  input  in_2,
  output out_3,
  output out_4,
  output out_5,
  output out_6
);

  wire not_1_out;

  and and_1 (out_3, in_2, in_1);
  not not_1 (not_1_out, in_1);
  and and_2 (out_4, in_2, not_1_out);

  assign out_5 = 1'b0;
  assign out_6 = in_1;
endmodule
