// Logisim project TP3-4.circ as structural Verilog: 1 circuit, main circuit main
module main (
  input  in_1,
  input  in_2,
  input  in_3,
  output out_4,
  output out_5,
  output out_6,
  output out_7,
  output out_8
);

  wire and_2_out, and_3_out, and_4_out, not_1_out, not_2_out, not_3_out;

  not not_1 (not_1_out, in_1);
  and and_1 (out_4, in_2, in_1);
  and and_2 (and_2_out, not_1_out, in_3, in_2);
  not not_2 (not_2_out, in_2);
  and and_3 (and_3_out, not_2_out, in_1);
  or or_1 (out_5, and_2_out, and_2_out, and_3_out);
  not not_3 (not_3_out, in_3);
  and and_4 (and_4_out, not_3_out, in_2);
  xor xor_1 (out_6, in_1, and_4_out);
  xor xor_2 (out_7, in_2, in_3);

  assign out_8 = in_3;
endmodule
