// Logisim project tp4-ex1.circ as structural Verilog
module main (
  input  in_1,
  input  in_2,
  input  in_3,
  output out_4,
  output out_5,
  output out_6,
  output out_7
);

  z1 z1_1 (.in_1(in_1), .in_2(in_2), .in_3(in_3), .out_4(out_4));
  z2 z2_1 (.in_1(in_1), .in_2(in_2), .in_3(in_3), .out_4(out_5));
  not not_1 (out_6, out_4);
  not not_2 (out_7, out_5);
endmodule

module z1 (
  input  in_1,
  input  in_2,
  input  in_3,
  output out_4
);

  wire and_1_out, and_2_out, and_3_out, not_1_out, not_2_out, not_3_out;

  not not_1 (not_1_out, in_1);
  not not_2 (not_2_out, in_2);
  not not_3 (not_3_out, in_3);
  and and_1 (and_1_out, not_1_out, not_2_out);
  and and_2 (and_2_out, not_1_out, in_2, not_3_out);
  and and_3 (and_3_out, not_2_out, not_3_out);
  or or_1 (out_4, and_1_out, and_2_out, and_3_out);
endmodule

module z2 (
  input  in_1,
  input  in_2,
  input  in_3,
  output out_4
);

  wire and_1_out, and_2_out, and_3_out, and_4_out, not_1_out, not_2_out, not_3_out;

  not not_1 (not_1_out, in_1);
  not not_2 (not_2_out, in_2);
  not not_3 (not_3_out, in_3);
  and and_1 (and_1_out, in_3, in_2, not_1_out);
  and and_2 (and_2_out, not_1_out, not_2_out, not_3_out);
  and and_3 (and_3_out, in_1, not_2_out, in_3);
  and and_4 (and_4_out, in_1, in_2, not_3_out);
  or or_1 (out_4, and_1_out, and_2_out, and_3_out, and_4_out);
endmodule
