// Logisim project tp4-ex3.circ as structural Verilog: 3 circuits, main circuit main
module main (
  input  in_1,
  input  in_2,
  input  in_3,
  input  in_4,
  input  in_5,
  input  in_6,
  output out_7
);

  wire and_1_out, and_2_out, and_3_out, and_4_out, and_5_out, and_6_out, and_7_out, and_8_out, not_1_out,
       not_2_out, not_3_out, not_4_out;

  and and_1 (and_1_out, not_1_out, in_6);
  and and_2 (and_2_out, not_3_out, not_2_out);
  not not_1 (not_1_out, in_5);
  not not_2 (not_2_out, in_6);
  not not_3 (not_3_out, in_5);
  and and_3 (and_3_out, in_5, not_4_out);
  not not_4 (not_4_out, in_6);
  and and_4 (and_4_out, in_5, in_6);
  and and_5 (and_5_out, in_1, and_2_out);
  and and_6 (and_6_out, in_2, and_1_out);
  and and_7 (and_7_out, in_3, and_3_out);
  and and_8 (and_8_out, in_4, and_4_out);
  or or_1 (out_7, and_5_out, and_6_out, and_7_out, and_8_out);
endmodule

module multiplexeur_1_2 (
  input  in_1,
  input  in_2,
  input  in_3,
  output out_4
);

  wire and_1_out, and_2_out, not_1_out;

  not not_1 (not_1_out, in_3);
  and and_1 (and_1_out, in_1, not_1_out);
  and and_2 (and_2_out, in_2, in_3);
  or or_1 (out_4, and_1_out, and_2_out);
endmodule

module multiplexeur_2_4 (
  input  in_1,
  input  in_2,
  input  in_3,
  input  in_4,
  input  in_5,
  input  in_6,
  output out_7
);

  wire multiplexeur_1_2_1_out_4, multiplexeur_1_2_2_out_4;

  multiplexeur_1_2 multiplexeur_1_2_1 (.in_1(in_1), .in_2(in_2), .in_3(in_6), .out_4(multiplexeur_1_2_1_out_4));
  multiplexeur_1_2 multiplexeur_1_2_2 (.in_1(in_3), .in_2(in_4), .in_3(in_6), .out_4(multiplexeur_1_2_2_out_4));
  multiplexeur_1_2 multiplexeur_1_2_3 (
    .in_1(multiplexeur_1_2_1_out_4), .in_2(multiplexeur_1_2_2_out_4), .in_3(in_5), .out_4(out_7));
endmodule
