// Logisim project tp5-ex1.circ as structural Verilog: 1 circuit, main circuit main
module main (
  input  in_1,
  input  in_2,
  output out_3,
  output Q_prime
);

  wire and_1_out, and_2_out, not_1_out;

  not not_1 (not_1_out, in_2);
  and and_1 (and_1_out, not_1_out, in_1);
  and and_2 (and_2_out, in_1, in_2);
  nor nor_1 (out_3, and_1_out, Q_prime);
  nor nor_2 (Q_prime, out_3, and_2_out);

  // Notes on the sheet:
  //   CLK
  //   D
  //   Q
endmodule
