// Logisim project tp5-ex2.circ as structural Verilog: 1 circuit, main circuit main
module main (
  input  CLR
);

  wire and_1_out, clock_1_out, d_ff_1_q, not_1_out;

  Clock #(.lowDuration(100)) clock_1 (.out(clock_1_out));
  and and_1 (and_1_out, not_1_out, CLR);
  D_Flip_Flop d_ff_1 (.clk(clock_1_out), .D(and_1_out), .Q(d_ff_1_q));  // open: Qn, preset, en, reset
  not not_1 (not_1_out, d_ff_1_q);
  LED led_1 (.in(d_ff_1_q));
endmodule
