// Logisim project tp5-ex3.circ as structural Verilog: 2 circuits, main circuit main
module main (
  input  A,
  input  P1,
  input  P2,
  input  P3,
  output P1_prime,
  output P2_prime,
  output P3_prime
);

  wire and_1_out, and_2_out;

  and and_1 (and_1_out, P1, P2, P3);
  and and_2 (and_2_out, P2, P3);
  or or_1 (P1_prime, A, and_1_out);
  or or_2 (P2_prime, P1, and_2_out);
  or or_3 (P3_prime, P2, P3);
endmodule

module ex3_2 (
  input  A,
  input  CLR
);

  wire and_1_out, and_2_out, and_3_out, clock_1_out, d_ff_1_q, d_ff_2_q, d_ff_3_q, main_1_p1_prime,
       main_1_p2_prime, main_1_p3_prime;

  Clock #(.lowDuration(100)) clock_1 (.out(clock_1_out));
  main main_1 (
    .A(A), .P1(and_3_out), .P2(and_2_out), .P3(and_1_out), .P1_prime(main_1_p1_prime),
    .P2_prime(main_1_p2_prime), .P3_prime(main_1_p3_prime));
  and and_1 (and_1_out, d_ff_3_q, CLR);
  and and_2 (and_2_out, d_ff_2_q, CLR);
  D_Flip_Flop d_ff_1 (.clk(clock_1_out), .D(main_1_p1_prime), .Q(d_ff_1_q));  // open: Qn, preset, en, reset
  D_Flip_Flop d_ff_2 (.clk(clock_1_out), .D(main_1_p2_prime), .Q(d_ff_2_q));  // open: Qn, preset, en, reset
  D_Flip_Flop d_ff_3 (.clk(clock_1_out), .D(main_1_p3_prime), .Q(d_ff_3_q));  // open: Qn, preset, en, reset
  and and_3 (and_3_out, d_ff_1_q, CLR);
  LED led_1 (.in(d_ff_1_q));
  LED led_2 (.in(d_ff_2_q));
  LED led_3 (.in(d_ff_3_q));

  // Notes on the sheet:
  //   CLK
endmodule
