// Logisim project tp5-ex4.circ as structural Verilog: 2 circuits, main circuit main
module main (
  input  X1,
  input  X0,
  input  E1,
  input  E0,
  output S1,
  output S0
);

  wire and_1_out, and_2_out, and_3_out, and_4_out, and_5_out, and_6_out, and_7_out, and_8_out, and_9_out,
       not_1_out, not_2_out, not_3_out, not_4_out, not_5_out;

  and and_1 (and_1_out, X1, X0);
  and and_2 (and_2_out, X0, E0);
  not not_1 (not_1_out, X1);
  and and_3 (and_3_out, not_1_out, E1);
  and and_4 (and_4_out, E1, E0);
  and and_5 (and_5_out, X1, X0);
  not not_2 (not_2_out, X1);
  and and_6 (and_6_out, not_2_out, not_3_out, E0);
  not not_3 (not_3_out, X0);
  and and_7 (and_7_out, X1, E1, not_4_out);
  not not_4 (not_4_out, E0);
  and and_8 (and_8_out, X0, E1);
  and and_9 (and_9_out, X0, not_5_out);
  not not_5 (not_5_out, E0);
  or or_1 (S0, and_5_out, and_6_out, and_7_out, and_8_out, and_9_out);
  or or_2 (S1, and_1_out, and_2_out, and_3_out, and_4_out);
endmodule

module ex4_2 (
  input  X1,
  input  X0,
  input  in_3
);

  wire and_1_out, and_2_out, and_3_out, clock_1_out, d_ff_1_q, d_ff_2_q, d_ff_3_q, main_1_s0, main_1_s1;

  Clock clock_1 (.out(clock_1_out));
  main main_1 (.X1(X1), .X0(X0), .E1(d_ff_1_q), .E0(d_ff_2_q), .S1(main_1_s1), .S0(main_1_s0));
  and and_1 (and_1_out, main_1_s1, in_3);
  and and_2 (and_2_out, main_1_s0, in_3);
  and and_3 (and_3_out, d_ff_2_q, d_ff_1_q);
  LED led_1 (.in(d_ff_1_q));
  D_Flip_Flop d_ff_1 (.clk(clock_1_out), .D(and_1_out), .Q(d_ff_1_q));  // open: Qn, preset, en, reset
  D_Flip_Flop d_ff_2 (.clk(clock_1_out), .D(and_2_out), .Q(d_ff_2_q));  // open: Qn, preset, en, reset
  D_Flip_Flop d_ff_3 (.clk(clock_1_out), .D(and_3_out), .Q(d_ff_3_q));  // open: Qn, preset, en, reset
  LED led_2 (.in(d_ff_2_q));
  LED led_3 (.in(d_ff_3_q));

  // Notes on the sheet:
  //   S1
  //   S0
  //   ALARME
endmodule
